// Logisim project ALU.circ as structural Verilog: 1 circuit, main circuit Ida ALU
// ALU
module Ida_ALU (
  input  [23:0] ALU_Source_1,
  input  [23:0] ALU_Source_2,
  input  [3:0] Operation,
  output [23:0] ALU_Result
);

  wire [1:0] Sgn, Usn;
  wire [4:0] bit_extender_1_out;
  wire [23:0] Add, And, Ar, bit_extender_2_out, bit_extender_3_out, Lr, Or, Rl, Rr, Sll, Sub, Xor;

  // Probe on ALU_Source_1
  // Probe on ALU_Source_2
  // Probe on Operation
  // Probe on ALU_Result
  Bit_Extender #(.in_width(24), .out_width(5)) bit_extender_1 (.in(ALU_Source_2), .out(bit_extender_1_out));
  Adder #(.width(24)) adder_1 (.a(ALU_Source_1), .b(ALU_Source_2), .out(Add));  // open: cin, cout
  Subtractor #(.width(24)) subtractor_1 (.a(ALU_Source_1), .b(ALU_Source_2), .out(Sub));  // open: bin, bout
  assign And = ALU_Source_1 & ALU_Source_2;  // AND_Gate and_1, 24 bits wide
  assign Or = ALU_Source_1 | ALU_Source_2;  // OR_Gate or_1, 24 bits wide
  assign Xor = ALU_Source_1 ^ ALU_Source_2;  // XOR_Gate xor_1, 24 bits wide
  Comparator #(.width(24)) comparator_1 (.a(ALU_Source_1), .b(ALU_Source_2), .gt(Sgn[1]), .eq(Sgn[0]));  // open: lt
  Shifter #(.width(24)) shifter_1 (.in(ALU_Source_1), .\dist (bit_extender_1_out), .out(Sll));
  Multiplexer #(.select(4), .width(24)) multiplexer_1 (
    .in0(Sll), .in1(Lr), .in2(Ar), .in3(Rl), .in4(Rr), .in5(And), .in6(Or), .in7(Xor), .in8(Add), .in9(Sub),
    .in10(Add), .in11(Add), .in12(bit_extender_2_out), .in13(bit_extender_3_out), .in14({24{1'b0}}),
    .in15({24{1'b0}}), .out(ALU_Result), .sel(Operation));  // open: en
  Shifter #(.width(24), .shift("lr")) shifter_2 (.in(ALU_Source_1), .\dist (bit_extender_1_out), .out(Lr));
  Shifter #(.width(24), .shift("ar")) shifter_3 (.in(ALU_Source_1), .\dist (bit_extender_1_out), .out(Ar));
  Shifter #(.width(24), .shift("rl")) shifter_4 (.in(ALU_Source_1), .\dist (bit_extender_1_out), .out(Rl));
  Shifter #(.width(24), .shift("rr")) shifter_5 (.in(ALU_Source_1), .\dist (bit_extender_1_out), .out(Rr));
  Comparator #(.width(24), .mode("unsigned")) comparator_2 (
    .a(ALU_Source_1), .b(ALU_Source_2), .gt(Usn[1]), .eq(Usn[0]));  // open: lt
  assign bit_extender_2_out = {{22{1'b0}}, Sgn};  // Bit_Extender bit_extender_2
  assign bit_extender_3_out = {{22{1'b0}}, Usn};  // Bit_Extender bit_extender_3

  // Other names for the same wires on the sheet: op[3:0] = Operation; result[23:0] = ALU_Result;
  //   s1[23:0] = ALU_Source_1; s2[23:0] = ALU_Source_2

  // Notes on the sheet:
  //   INPUTS
  //   INPUT PROBES
  //   DO NOT MOVE/ADD/CHANGE ANY INPUT OR OUTPUT PINS!
  //   OUTPUT PROBES
  //   OUTPUT
endmodule
