// Logisim project CPU.circ as structural Verilog
// CPU
module Ida_CPU (
  input  [31:0] Instruction,
  input  Clock,
  output [23:0] Mem_Data,
  output [23:0] Mem_Address,
  output Mem_Write,
  output [23:0] Next_PC,
  output [23:0] r00,
  output [23:0] r01,
  output [23:0] r02,
  output [23:0] r03,
  output [23:0] r04,
  output [23:0] r05,
  output [23:0] r06,
  output [23:0] r07,
  output [23:0] r08,
  output [23:0] r09,
  output [23:0] r10,
  output [23:0] r11,
  output [23:0] r12,
  output [23:0] r13,
  output [23:0] r14,
  output [23:0] r15
);

  wire comparator_1_eq, comparator_2_eq, control_1_cr, control_1_mem__ld, control_1_rg__wr;
  wire [1:0] control_1_cr_val, CR_q;
  wire [3:0] multiplexer_1_out, prep_jmp_1_jmp;
  wire [15:0] bit_extender_1_out;
  wire [19:0] bit_extender_2_out;
  wire [23:0] bit_extender_3_out, bit_extender_4_out, control_1_nxt_pc, control_1_rg_val,
       ida_alu_1_alu_result, ida_register_file_1_reg_1_value, ida_register_file_1_reg_2_value,
       ida_register_file_1_reg_3_value, multiplexer_2_out, multiplexer_3_out, multiplexer_4_out,
       multiplexer_5_out, prep_jmp_1_jmp_adr, ram_1_data;
  wire [31:0] Cur_inst, jmp_taken_1_out_inst, register_1_q;

  // Probe on Instruction
  // Probe on Clock
  // Probe on r00
  // Probe on r01
  // Probe on r02
  // Probe on r03
  // Probe on r04
  // Probe on r05
  // Probe on r06
  // Probe on r07
  // Probe on Mem_Data
  // Probe on Mem_Address
  // Probe on Mem_Write
  // Probe on Next_PC
  // Probe on r08
  // Probe on r09
  // Probe on r10
  // Probe on r11
  // Probe on r12
  // Probe on r13
  // Probe on r14
  // Probe on r15
  Register #(.width(32)) register_1 (.D(jmp_taken_1_out_inst), .Q(register_1_q), .clk(Clock));  // open: en, clr
  JMP_TAKEN jmp_taken_1 (.JMP(Cur_inst), .INST(Instruction), .OUT_INST(jmp_taken_1_out_inst));
  CQ_JUMP cq_jump_1 (.Reg_INSTR(register_1_q), .CR(CR_q), .Output(Cur_inst));
  Bit_Extender #(.in_width(24)) bit_extender_1 (.in(Cur_inst[23:0]), .out(bit_extender_1_out));
  Bit_Extender #(.in_width(24), .out_width(20)) bit_extender_2 (.in(Cur_inst[23:0]), .out(bit_extender_2_out));
  Register #(.width(2)) CR (.D(control_1_cr_val), .en(control_1_cr), .Q(CR_q), .clk(Clock));  // open: clr
  Ida_Register_File ida_register_file_1 (
    .Read_Reg_1(Cur_inst[19:16]), .Read_Reg_2(Cur_inst[3:0]), .Write_Reg(multiplexer_1_out),
    .Write_Value(control_1_rg_val), .Reg_1_Value(ida_register_file_1_reg_1_value),
    .Reg_2_Value(ida_register_file_1_reg_2_value), .Reg_Write(control_1_rg__wr), .Clock(Clock), .r00(r00),
    .r01(r01), .r02(r02), .r03(r03), .r04(r04), .r05(r05), .r06(r06), .r07(r07), .r08(r08), .r09(r09),
    .r10(r10), .r11(r11), .r12(r12), .r13(r13), .r14(r14), .r15(r15),
    .Reg_3_Value(ida_register_file_1_reg_3_value));
  Multiplexer #(.width(4)) multiplexer_1 (
    .in0(Cur_inst[23:20]), .in1(4'b0010), .out(multiplexer_1_out), .sel(comparator_1_eq));  // open: en
  Comparator #(.width(4)) comparator_1 (.a(Cur_inst[31:28]), .b(4'b1110), .eq(comparator_1_eq));  // open: gt, lt
  assign bit_extender_3_out = {{8{bit_extender_1_out[15]}}, bit_extender_1_out};  // Bit_Extender bit_extender_3
  assign bit_extender_4_out = {{4{bit_extender_2_out[19]}}, bit_extender_2_out};  // Bit_Extender bit_extender_4
  Multiplexer #(.select(4), .width(24)) multiplexer_2 (
    .in0(bit_extender_3_out), .in1(bit_extender_3_out), .in2(bit_extender_3_out), .in3(bit_extender_3_out),
    .in4(bit_extender_3_out), .in5(bit_extender_3_out), .in6(bit_extender_3_out), .in7(bit_extender_3_out),
    .in8(bit_extender_3_out), .in9(bit_extender_3_out), .in10(bit_extender_3_out), .in11(bit_extender_3_out),
    .in12(bit_extender_4_out), .in13(bit_extender_4_out), .in14(Cur_inst[23:0]), .in15(Cur_inst[23:0]),
    .out(multiplexer_2_out), .sel(Cur_inst[31:28]));  // open: en
  // Probe on bit_extender_3_out
  // Probe on bit_extender_4_out
  Multiplexer #(.width(24)) multiplexer_3 (
    .in0(ida_register_file_1_reg_1_value), .in1(ida_register_file_1_reg_3_value), .out(multiplexer_3_out),
    .sel(control_1_cr));  // open: en
  Multiplexer #(.width(24)) multiplexer_4 (
    .in0(ida_register_file_1_reg_2_value), .in1(multiplexer_2_out), .out(multiplexer_4_out),
    .sel(Cur_inst[24]));  // open: en
  Ida_ALU ida_alu_1 (
    .ALU_Source_1(multiplexer_3_out), .ALU_Source_2(multiplexer_4_out), .Operation(Cur_inst[31:28]),
    .ALU_Result(ida_alu_1_alu_result));
  PREP_JMP prep_jmp_1 (
    .CUR_INST(Cur_inst), .RA(ida_register_file_1_reg_2_value), .JMP(prep_jmp_1_jmp),
    .JMP_ADR(prep_jmp_1_jmp_adr));
  Control control_1 (
    .Current_Instruction(Cur_inst[31:28]), .ALU_out(ida_alu_1_alu_result), .CR_VAL(control_1_cr_val),
    .CR(control_1_cr), .RI(multiplexer_4_out), .RG__WR(control_1_rg__wr), .RG_VAL(control_1_rg_val),
    .MEM_ADR(Mem_Address), .MEM_STR(Mem_Data), .RD_VAL(ida_register_file_1_reg_3_value),
    .MEM__STR(Mem_Write), .MEM__LD(control_1_mem__ld), .MEM_LD(ram_1_data), .NXT_PC(control_1_nxt_pc),
    .INST_ADR(Next_PC));
  RAM #(.addrWidth(24), .dataWidth(24), .bus("separate")) ram_1 (
    .addr(Mem_Address), .din(Mem_Data), .data(ram_1_data), .str(Mem_Write), .sel(1'b1), .clk(Clock),
    .ld(control_1_mem__ld));  // open: clr
  Comparator #(.width(4)) comparator_2 (.a(4'b1111), .b(prep_jmp_1_jmp), .eq(comparator_2_eq));  // open: gt, lt
  Multiplexer #(.width(24)) multiplexer_5 (
    .in0(control_1_nxt_pc), .in1(prep_jmp_1_jmp_adr), .out(multiplexer_5_out), .sel(comparator_2_eq));  // open: en
  Register #(.width(24)) register_2 (.D(multiplexer_5_out), .Q(Next_PC), .clk(Clock));  // open: en, clr

  // Other names for the same wires on the sheet: clk = Clock; op[3:0] = Cur_inst[31:28]; inst[31:0] = Instruction;
  //   memAddr[23:0] = Mem_Address; memData[23:0] = Mem_Data; memWrite = Mem_Write; nextPC[23:0] = Next_PC

  // Notes on the sheet:
  //   INPUTS
  //   INPUT PROBES
  //   OUTPUT PROBES
  //   OUTPUTS
  //   DO NOT MOVE/ADD/CHANGE ANY INPUT OR OUTPUT PINS!
endmodule

module CQ_JUMP (
  input  [1:0] CR,
  input  [31:0] Reg_INSTR,
  output [31:0] Output
);

  wire comparison_only_1_out_3;

  Comparison_ONLY comparison_only_1 (.in_1(Reg_INSTR[27:25]), .out_3(comparison_only_1_out_3), .in_2(CR));
  Multiplexer #(.width(32)) multiplexer_1 (
    .in0({32{1'b0}}), .in1(Reg_INSTR), .out(Output), .sel(comparison_only_1_out_3));  // open: en
endmodule

module Comparison_ONLY (
  input  [2:0] in_1,
  input  [1:0] in_2,
  output out_3
);

  wire and_1_out, not_1_out, not_2_out, not_3_out, not_4_out, or_1_out, or_2_out;

  not not_1 (not_1_out, in_2[0]);
  not not_2 (not_2_out, in_2[1]);
  and and_1 (and_1_out, not_3_out, not_4_out);
  or or_1 (or_1_out, in_2[0], not_2_out);
  Multiplexer #(.select(3)) multiplexer_1 (
    .in0(1'b0), .in1(or_1_out), .in2(in_2[1]), .in3(not_1_out), .in4(in_2[0]), .in5(or_2_out),
    .in6(and_1_out), .in7(1'b1), .out(out_3), .sel(in_1));  // open: en
  not not_3 (not_3_out, in_2[1]);
  not not_4 (not_4_out, in_2[0]);
  or or_2 (or_2_out, in_2[1], in_2[0]);

  // Other names for the same wires on the sheet: Eq = in_2[0]; GT_LT = in_2[1]
endmodule

module Control (
  input  [23:0] INST_ADR,
  input  [23:0] RI,
  input  [23:0] ALU_out,
  input  [3:0] Current_Instruction,
  input  [23:0] RD_VAL,
  input  [23:0] MEM_LD,
  output [1:0] CR_VAL,
  output CR,
  output [23:0] NXT_PC,
  output RG__WR,
  output [23:0] RG_VAL,
  output [23:0] MEM_ADR,
  output [23:0] MEM_STR,
  output MEM__STR,
  output MEM__LD
);

  wire comparator_1_eq, comparator_1_lt, comparator_2_gt, comparator_3_gt, comparator_3_lt, or_2_out,
       or_3_out;
  wire [1:0] bitadder_1_out;

  and and_1 (CR, comparator_1_lt, comparator_2_gt);
  or or_1 (RG__WR, comparator_3_lt, or_3_out);
  Multiplexer #(.select(2), .width(24)) multiplexer_1 (
    .in0(ALU_out), .in1(MEM_LD), .in2(RI), .in3({24{1'b0}}), .out(RG_VAL), .sel(bitadder_1_out));  // open: en
  BitAdder #(.width(1)) bitadder_1 (.in0(or_2_out), .in1(comparator_1_eq), .out(bitadder_1_out));
  or or_2 (or_2_out, comparator_3_gt, MEM__LD);
  or or_3 (or_3_out, MEM__LD, comparator_1_eq);
  Comparator #(.width(4), .mode("unsigned")) comparator_1 (
    .a(Current_Instruction), .b(4'b1110), .eq(comparator_1_eq), .lt(comparator_1_lt));  // open: gt
  Comparator #(.width(4), .mode("unsigned")) comparator_2 (
    .a(Current_Instruction), .b(4'b1011), .gt(comparator_2_gt), .eq(MEM__STR));  // open: lt
  Comparator #(.width(4), .mode("unsigned")) comparator_3 (
    .a(Current_Instruction), .b(4'b1010), .gt(comparator_3_gt), .eq(MEM__LD), .lt(comparator_3_lt));
  Adder #(.width(24)) adder_1 (.a(INST_ADR), .b(24'h1), .out(NXT_PC));  // open: cin, cout

  assign CR_VAL = ALU_out[1:0];
  assign MEM_ADR = ALU_out;
  assign MEM_STR = RD_VAL;
endmodule

module JMP_TAKEN (
  input  [31:0] JMP,
  input  [31:0] INST,
  output [31:0] OUT_INST
);

  wire comparator_1_eq;

  Multiplexer #(.width(32), .enable("false")) multiplexer_1 (
    .in0(INST), .in1({32{1'b0}}), .out(OUT_INST), .sel(comparator_1_eq));
  Comparator #(.width(4), .mode("unsigned")) comparator_1 (
    .a(4'b1111), .b(JMP[31:28]), .eq(comparator_1_eq));  // open: gt, lt
endmodule

module PREP_JMP (
  input  [31:0] CUR_INST,
  input  [23:0] RA,
  output [3:0] JMP,
  output [23:0] JMP_ADR
);

  Multiplexer #(.width(24)) multiplexer_1 (
    .in0(RA), .in1(CUR_INST[23:0]), .out(JMP_ADR), .sel(CUR_INST[24]));  // open: en

  assign JMP = CUR_INST[31:28];
endmodule
