// Logisim project REG.circ as structural Verilog: 1 circuit, main circuit Ida Register File
// Register File
module Ida_Register_File (
  input  [3:0] Read_Reg_1,
  input  [3:0] Read_Reg_2,
  input  [3:0] Write_Reg,
  input  [23:0] Write_Value,
  input  Reg_Write,
  input  Clock,
  output [23:0] Reg_1_Value,
  output [23:0] Reg_2_Value,
  output [23:0] Reg_3_Value,
  output [23:0] r00,
  output [23:0] r01,
  output [23:0] r02,
  output [23:0] r03,
  output [23:0] r04,
  output [23:0] r05,
  output [23:0] r06,
  output [23:0] r07,
  output [23:0] r08,
  output [23:0] r09,
  output [23:0] r10,
  output [23:0] r11,
  output [23:0] r12,
  output [23:0] r13,
  output [23:0] r14,
  output [23:0] r15
);

  wire demultiplexer_1_out0, demultiplexer_1_out1, demultiplexer_1_out2, demultiplexer_1_out3,
       demultiplexer_1_out4, demultiplexer_1_out5, demultiplexer_1_out6, demultiplexer_1_out7,
       demultiplexer_1_out8, demultiplexer_1_out9, demultiplexer_1_out10, demultiplexer_1_out11,
       demultiplexer_1_out12, demultiplexer_1_out13, demultiplexer_1_out14, demultiplexer_1_out15, en00,
       en01, en02, en03, en04, en05, en06, en07, en08, en09, en10, en11, en12, en13, en14, en15;
  wire [23:0] wr00, wr01, wr02, wr03, wr04, wr05, wr06, wr07, wr08, wr09, wr10, wr11, wr12, wr13, wr14, wr15;

  // Probe on Read_Reg_1
  // Probe on Read_Reg_2
  // Probe on Write_Reg
  // Probe on Write_Value
  // Probe on Reg_Write
  // Probe on Clock
  // Probe on Reg_1_Value
  // Probe on Reg_2_Value
  // Probe on Reg_3_Value
  // Probe on r00
  // Probe on r01
  // Probe on r02
  // Probe on r03
  // Probe on r04
  // Probe on r05
  // Probe on r06
  // Probe on r07
  // Probe on r08
  // Probe on r09
  // Probe on r10
  // Probe on r11
  // Probe on r12
  // Probe on r13
  // Probe on r14
  // Probe on r15
  Demultiplexer #(.select(4)) demultiplexer_1 (
    .out0(demultiplexer_1_out0), .out1(demultiplexer_1_out1), .out2(demultiplexer_1_out2),
    .out3(demultiplexer_1_out3), .out4(demultiplexer_1_out4), .out5(demultiplexer_1_out5),
    .out6(demultiplexer_1_out6), .out7(demultiplexer_1_out7), .out8(demultiplexer_1_out8),
    .out9(demultiplexer_1_out9), .out10(demultiplexer_1_out10), .out11(demultiplexer_1_out11),
    .out12(demultiplexer_1_out12), .out13(demultiplexer_1_out13), .out14(demultiplexer_1_out14),
    .out15(demultiplexer_1_out15), .in(1'b1), .sel(Write_Reg));  // open: en
  Demultiplexer #(.select(4), .width(24)) demultiplexer_2 (
    .out0(wr00), .out1(wr01), .out2(wr02), .out3(wr03), .out4(wr04), .out5(wr05), .out6(wr06), .out7(wr07),
    .out8(wr08), .out9(wr09), .out10(wr10), .out11(wr11), .out12(wr12), .out13(wr13), .out14(wr14),
    .out15(wr15), .in(Write_Value), .sel(Write_Reg));  // open: en
  and and_1 (en00, demultiplexer_1_out0, Reg_Write);
  and and_2 (en02, demultiplexer_1_out2, Reg_Write);
  and and_3 (en04, demultiplexer_1_out4, Reg_Write);
  and and_4 (en06, demultiplexer_1_out6, Reg_Write);
  and and_5 (en08, demultiplexer_1_out8, Reg_Write);
  and and_6 (en10, demultiplexer_1_out10, Reg_Write);
  and and_7 (en12, demultiplexer_1_out12, Reg_Write);
  and and_8 (en14, demultiplexer_1_out14, Reg_Write);
  and and_9 (en01, demultiplexer_1_out1, Reg_Write);
  and and_10 (en03, demultiplexer_1_out3, Reg_Write);
  and and_11 (en05, demultiplexer_1_out5, Reg_Write);
  and and_12 (en07, demultiplexer_1_out7, Reg_Write);
  and and_13 (en09, demultiplexer_1_out9, Reg_Write);
  and and_14 (en11, demultiplexer_1_out11, Reg_Write);
  and and_15 (en13, demultiplexer_1_out13, Reg_Write);
  and and_16 (en15, demultiplexer_1_out15, Reg_Write);
  Register #(.width(24)) Reg00 (.D(wr00), .en(1'b0), .Q(r00), .clk(Clock));  // open: clr
  Register #(.width(24)) Reg04 (.D(wr04), .en(en04), .Q(r04), .clk(Clock));  // open: clr
  Register #(.width(24)) Reg08 (.D(wr08), .en(en08), .Q(r08), .clk(Clock));  // open: clr
  Register #(.width(24)) Reg12 (.D(wr12), .en(en12), .Q(r12), .clk(Clock));  // open: clr
  Register #(.width(24)) Reg01 (.D(wr01), .en(en01), .Q(r01), .clk(Clock));  // open: clr
  Register #(.width(24)) Reg05 (.D(wr05), .en(en05), .Q(r05), .clk(Clock));  // open: clr
  Register #(.width(24)) Reg09 (.D(wr09), .en(en09), .Q(r09), .clk(Clock));  // open: clr
  Register #(.width(24)) Reg13 (.D(wr13), .en(en13), .Q(r13), .clk(Clock));  // open: clr
  Register #(.width(24)) Reg02 (.D(wr02), .en(en02), .Q(r02), .clk(Clock));  // open: clr
  Register #(.width(24)) Reg06 (.D(wr06), .en(en06), .Q(r06), .clk(Clock));  // open: clr
  Register #(.width(24)) Reg10 (.D(wr10), .en(en10), .Q(r10), .clk(Clock));  // open: clr
  Register #(.width(24)) Reg14 (.D(wr14), .en(en14), .Q(r14), .clk(Clock));  // open: clr
  Register #(.width(24)) Reg03 (.D(wr03), .en(en03), .Q(r03), .clk(Clock));  // open: clr
  Register #(.width(24)) Reg07 (.D(wr07), .en(en07), .Q(r07), .clk(Clock));  // open: clr
  Register #(.width(24)) Reg11 (.D(wr11), .en(en11), .Q(r11), .clk(Clock));  // open: clr
  Register #(.width(24)) Reg15 (.D(wr15), .en(en15), .Q(r15), .clk(Clock));  // open: clr
  Multiplexer #(.select(4), .width(24)) multiplexer_1 (
    .in0(r00), .in1(r01), .in2(r02), .in3(r03), .in4(r04), .in5(r05), .in6(r06), .in7(r07), .in8(r08),
    .in9(r09), .in10(r10), .in11(r11), .in12(r12), .in13(r13), .in14(r14), .in15(r15), .out(Reg_1_Value),
    .sel(Read_Reg_1));  // open: en
  Multiplexer #(.select(4), .width(24)) multiplexer_2 (
    .in0(r00), .in1(r01), .in2(r02), .in3(r03), .in4(r04), .in5(r05), .in6(r06), .in7(r07), .in8(r08),
    .in9(r09), .in10(r10), .in11(r11), .in12(r12), .in13(r13), .in14(r14), .in15(r15), .out(Reg_2_Value),
    .sel(Read_Reg_2));  // open: en
  Multiplexer #(.select(4), .width(24)) multiplexer_3 (
    .in0(r00), .in1(r01), .in2(r02), .in3(r03), .in4(r04), .in5(r05), .in6(r06), .in7(r07), .in8(r08),
    .in9(r09), .in10(r10), .in11(r11), .in12(r12), .in13(r13), .in14(r14), .in15(r15), .out(Reg_3_Value),
    .sel(Write_Reg));  // open: en

  // Other names for the same wires on the sheet: clk = Clock; reg1Read[3:0] = Read_Reg_1; reg1Val[23:0] = Reg_1_Value;
  //   reg2Read[3:0] = Read_Reg_2; reg2Val[23:0] = Reg_2_Value; reg3Val[23:0] = Reg_3_Value;
  //   reg3Write[3:0] = Write_Reg; write = Reg_Write; writeVal[23:0] = Write_Value

  // Notes on the sheet:
  //   INPUT PINS
  //   INPUT PROBES
  //   OUTPUT PROBES
  //   OUTPUT PINS
  //   DO NOT MOVE/ADD/CHANGE ANY INPUT OR OUTPUT PINS!
endmodule
